# Fritzing sketch Çakar Devresi (saved by Fritzing 0.9.3b)
breadboards: 1

parts:
  Parça1 = Arduino Uno (Rev3)
  R1 = Resistor [tolerance=±5% resistance=220 package=THT]
  LED1 = smd LED [color="Red (633nm)" package="1206 [SMD]"]
  LED2 = smd LED [color="Red (633nm)" package="1206 [SMD]"]
  R2 = Resistor [tolerance=±5% resistance=220 package=THT]

nets:
  N1: Parça1.D12/MISO, LED1.anode
  N2: Parça1.D13/SCK, LED2.anode
  N3: Parça1.GND, R1.Pin_0, R2.Pin_0
  N4: R1.Pin_1, LED1.cathode
  N5: LED2.cathode, R2.Pin_1
