# Fritzing sketch Transistor (saved by Fritzing 0.9.3b)
breadboards: 1

parts:
  Parça1 = Arduino Uno (Rev3)
  Q1 = NPN-Transistor [package="TO92 [THT]"]
  LED1 = LED - 5mm [color="Red (633nm)" package="5 mm [THT]"]  # not connected
  R1 = Resistor [tolerance=±5% resistance=220 package=THT]
  R2 = Resistor [tolerance=±5% resistance=220 package=THT]
  VCC1 = Battery block 9V

nets:
  N1: Parça1.D8, R2.Pin_0
  N2: Parça1.GND, Q1.B, VCC1.-
  N3: Q1.C, R2.Pin_1
  N4: R1.Pin_0, VCC1.+
