# Fritzing sketch Button (saved by Fritzing 0.9.3b)
breadboards: 1

parts:
  Parça1 = Arduino Uno (Rev3)
  S1 = Pushbutton [package="[THT]"]
  R1 = Resistor [tolerance=±5% resistance=220 package=THT]

nets:
  N1: Parça1.A0, S1.Pin_3, S1.Pin_4, R1.Pin_1
  N2: Parça1.5V, S1.Pin_1, S1.Pin_2
  N3: Parça1.GND, R1.Pin_0
