# Fritzing sketch Button_LED (saved by Fritzing 0.9.3b)
breadboards: 1

parts:
  Parça1 = Arduino Uno (Rev3)
  S1 = Pushbutton [package="[THT]"]
  R1 = Resistor [tolerance=±5% resistance=220 package=THT]
  LED1 = LED - 5mm [color="Red (633nm)" package="5 mm [THT]"]  # not connected
  R2 = Resistor [tolerance=±5% resistance=220 package=THT]

nets:
  N1: Parça1.A0, S1.Pin_3, S1.Pin_4, R1.Pin_1
  N2: Parça1.D8, R2.Pin_0
  N3: Parça1.5V, S1.Pin_1, S1.Pin_2
  N4: Parça1.GND, R1.Pin_0
