# Fritzing sketch RGB_LED (saved by Fritzing 0.9.3b)
breadboards: 1

parts:
  Parça1 = Arduino Uno (Rev3)
  LED1 = RGB LED (com. cathode, rgb) [package="5 mm [THT]"]

nets:
  N1: Parça1.D9_PWM, LED1.red_anode
  N2: Parça1.D10_PWM/SS, LED1.green_anode
  N3: Parça1.D11_PWM/MOSI, LED1.blue_anode
  N4: Parça1.5V, LED1.common_cathode
