# Fritzing sketch RGB_LED2 (saved by Fritzing 0.9.3b)
breadboards: 1

parts:
  Parça1 = Arduino Uno (Rev3)
  LED1 = RGB LED (com. cathode, rgb) [package="5 mm [THT]"]
  R1 = Rotary Potentiometer (Small) [maximum_resistance=100kΩ package=THT]
  R2 = Rotary Potentiometer (Small) [maximum_resistance=100kΩ package=THT]
  R3 = Rotary Potentiometer (Small) [maximum_resistance=100kΩ package=THT]

nets:
  N1: Parça1.A0, R1.wiper
  N2: Parça1.A1, R2.wiper
  N3: Parça1.A2, R3.wiper
  N4: Parça1.D9_PWM, LED1.red_anode
  N5: Parça1.D10_PWM/SS, LED1.green_anode
  N6: Parça1.D11_PWM/MOSI, LED1.blue_anode
  N7: Parça1.5V, LED1.common_cathode, R1.leg1, R2.leg1, R3.leg1
  N8: Parça1.GND, R1.leg2, R2.leg2, R3.leg2
