# Fritzing sketch LDR (saved by Fritzing 0.9.3b)
breadboards: 1

parts:
  Parça1 = Arduino Uno (Rev3)
  R1 = Photocell (LDR) [package=THT]
  R2 = Resistor [tolerance=±5% resistance=220 package=THT]

nets:
  N1: Parça1.A0, R1.pin_1, R2.Pin_0
  N2: Parça1.5V, R1.pin_0
  N3: Parça1.GND, R2.Pin_1
