# Fritzing sketch Buzzer (saved by Fritzing 0.9.3b)
breadboards: 1

parts:
  Parça1 = Arduino Uno (Rev3)
  J1 = Piezo Speaker
  R1 = Resistor [tolerance=±5% resistance=220 package=THT]

nets:
  N1: Parça1.D6_PWM, J1.pin2
  N2: Parça1.GND, R1.Pin_0
  N3: J1.pin1, R1.Pin_1
