# Fritzing sketch Yedi_Segment_Potans (saved by Fritzing 0.9.3b)
breadboards: 1

parts:
  Parça1 = Arduino Uno (Rev3)
  DI1 = 7-Segment LED Display [package=THT]
  R1 = Rotary Potentiometer (Small) [maximum_resistance=100kΩ package=THT]

nets:
  N1: Parça1.A0, R1.wiper
  N2: Parça1.D8, DI1.cathodeG
  N3: Parça1.D9_PWM, DI1.cathodeDP
  N4: Parça1.D2, DI1.cathodeA
  N5: Parça1.D3_PWM, DI1.cathodeB
  N6: Parça1.D4, DI1.cathodeC
  N7: Parça1.D5_PWM, DI1.cathodeD
  N8: Parça1.D6_PWM, DI1.cathodeE
  N9: Parça1.D7, DI1.cathodeF
  N10: Parça1.5V, DI1.commAnode#2, R1.leg1
  N11: Parça1.GND, R1.leg2
