# Fritzing sketch Yedi_Segment (saved by Fritzing 0.9.3b)
breadboards: 1

parts:
  Parça1 = Arduino Uno (Rev3)
  DI1 = 7-Segment LED Display [package=THT]

nets:
  N1: Parça1.D8, DI1.cathodeG
  N2: Parça1.D9_PWM, DI1.cathodeDP
  N3: Parça1.D2, DI1.cathodeA
  N4: Parça1.D3_PWM, DI1.cathodeB
  N5: Parça1.D4, DI1.cathodeC
  N6: Parça1.D5_PWM, DI1.cathodeD
  N7: Parça1.D6_PWM, DI1.cathodeE
  N8: Parça1.D7, DI1.cathodeF
  N9: Parça1.5V, DI1.commAnode#2
