# Fritzing sketch 7segment_1 (saved by Fritzing 0.9.1b)
breadboards: 1

parts:
  Eleman1 = Arduino Nano (Rev3.0)
  7_Segment1 = 7 Segment Display
  R1 = Resistor [tolerance=±5% resistance=220 package="0603 [SMD]"]

nets:
  N1: Eleman1.GND, R1.Pin_0
  N2: Eleman1.D2, 7_Segment1.Segment_C
  N3: Eleman1.D3, 7_Segment1.Segment_D
  N4: Eleman1.D4, 7_Segment1.Segment_E
  N5: Eleman1.D10, 7_Segment1.Segment_B
  N6: Eleman1.D11/MOSI, 7_Segment1.Segment_A
  N7: Eleman1.D12/MISO, 7_Segment1.Segment_F
  N8: Eleman1.D13/SCK, 7_Segment1.Segment_G
  N9: 7_Segment1.common_cathode, R1.Pin_1

// code stored in the sketch: __7segment_1.ino
// Seven segment display uzerindeki segmentelerin her birini sirasiyla <t> sn araliklarla yakan program
// Seven segment displayin Arduino'ya baglantilari;
byte a = 11; 
byte b = 10; 
byte c = 2; 
byte d = 3; 
byte e = 4; 
byte f = 12; 
byte g = 13;
int t = 100;
void setup() {
  pinMode(a, OUTPUT);
  pinMode(b, OUTPUT);
  pinMode(c, OUTPUT);
  pinMode(d, OUTPUT);
  pinMode(e, OUTPUT);
  pinMode(f, OUTPUT);
  pinMode(g, OUTPUT);
}

void loop() {
  digitalWrite(f, LOW);
  digitalWrite(a, HIGH);
  delay(t);
  digitalWrite(a, LOW);
  digitalWrite(b, HIGH);
  delay(t);
  digitalWrite(b, LOW);
  digitalWrite(c, HIGH);
  delay(t);
  digitalWrite(c, LOW);
  digitalWrite(d, HIGH);
  delay(t);
  digitalWrite(d, LOW);
  digitalWrite(e, HIGH);
  delay(t);
  digitalWrite(e, LOW);
  digitalWrite(f, HIGH);
  delay(t);
}
